// Digital circuit Constant Register.dig as structural Verilog
module Constant_Register (
  input  [2:0] Control,
  input  [7:0] MEM,
  output [7:0] MAIN,
  output [7:0] I
);

  Register #(.Bits(8)) register_1 (.D(MEM), .C(Control[0]), .en(1'b1), .Q(I));
  assign MAIN = ~Control[2] ? I : 8'bz;  // DriverInvSel driverinvsel_1

  // Notes on the sheet:
  //   Control: 0: Load Bus
  //   1: Load Mem
  //   2: Assert Main, default 1
endmodule
