// Digital circuit Address Register.dig as structural Verilog
module Address_Register (
  input  [6:0] Control,
  input  [15:0] xfer,
  output [15:0] ADDR,
  output [15:0] I
);

  wire and_1_out, and_2_out, delay_1_out, delay_2_out, delay_3_out, delay_4_out, nor_1_out, not_1_out,
       or_1_out, xor_1_out, xor_2_out, xor_3_out;
  wire [15:0] register_1_q, register_2_q;

  assign xfer = ~Control[6] ? register_1_q : 16'bz;  // DriverInvSel driverinvsel_1
  assign ADDR = ~Control[5] ? register_2_q : 16'bz;  // DriverInvSel driverinvsel_2
  Register #(.Bits(16)) register_1 (.D(I), .C(Control[0]), .en(1'b1), .Q(register_1_q));
  Register #(.Bits(16)) register_2 (.D(I), .C(Control[0]), .en(1'b1), .Q(register_2_q));
  not not_1 (not_1_out, Control[4]);
  Delay #(.delayTime(4)) delay_1 (.in(not_1_out), .out(delay_1_out));
  Delay #(.delayTime(4)) delay_2 (.in(Control[1]), .out(delay_2_out));
  and and_1 (and_1_out, Control[3], Control[2]);
  xor xor_1 (xor_1_out, not_1_out, delay_1_out);
  xor xor_2 (xor_2_out, Control[1], delay_2_out);
  xor xor_3 (xor_3_out, Control[3], Control[2]);
  or or_1 (or_1_out, and_1_out, not_1_out, Control[1]);
  nor nor_1 (nor_1_out, xor_1_out, xor_2_out);
  Delay #(.delayTime(3)) delay_3 (.in(xor_3_out), .out(delay_3_out));
  Delay #(.delayTime(4)) delay_4 (.in(Control[2]), .out(delay_4_out));
  and and_2 (and_2_out, or_1_out, nor_1_out);
  CounterPreset #(.Bits(16)) counterpreset_1 (
    .en(delay_3_out), .C(and_2_out), .dir(~delay_4_out), .in(xfer), .ld(not_1_out), .clr(Control[1]), .out(I));  // open: ovf

  // Other names for the same wires on the sheet: clock = Control[0]; Clear = Control[1]; Dec = Control[2];
  //   Inc = Control[3]; Load = Control[4]; A_Addr = Control[5]; A_Bus = Control[6]

  // Notes on the sheet:
  //   ADDR: Addr Bus
  //   Control: 0: Clock
  //   1: Clear
  //   2: Dec
  //   3: Inc
  //   4: Load
  //   5: Assert Addr
  //   6: Assert Bus, default 124
  //   xfer: default 1234
endmodule
