// Digital circuit Memory.dig as structural Verilog
module Memory (
  input  [15:0] ADDR,
  input  [3:0] Control,
  output [7:0] MEM
);

  RAMSinglePortSel #(.AddrBits(15), .Bits(8)) RAM (
    .A(ADDR[14:0]), .CS(ADDR[15]), .WE(~Control[1]), .OE(~Control[2]), .D(MEM));
  EEPROM #(.AddrBits(15), .isProgramMemory("true"), .Bits(8)) ROM (
    .A(ADDR[14:0]), .CS(~ADDR[15]), .WE(~1'b1), .OE(~Control[2]), .D(MEM));

  // Notes on the sheet:
  //   Control: 0: Assert
  //   1: Load
  //   2: Dir
  //   3: Ack, default 1
  //   contents of ROM (hex, n*v repeats v):
  //   1,2,3,4,5,6,7
  //   contents of ROM (hex, n*v repeats v):
  //   1,2,3,4,5,6,7
endmodule
