// Digital circuit Stage 2.dig as structural Verilog
module Stage_2 (
  input  [6:0] Flags,
  input  Clock,
  input  [7:0] PipeIn,
  output Break,
  output [7:0] Main,
  output [1:0] SPSIDI,
  output [2:0] Addr,
  output Bus_Request,
  output PCRA_Flip
);

  wire [7:0] _2A_d, _2B_d;

  ROM #(.AddrBits(15), .Bits(8)) _2A (.A({Flags, PipeIn}), .sel(1'b1), .D(_2A_d));
  ROM #(.AddrBits(15), .Bits(8)) _2B (.A({Flags, PipeIn}), .sel(1'b1), .D(_2B_d));
  Register #(.Bits(16)) register_1 (
    .D({_2B_d, _2A_d}), .C(Clock), .en(1'b1), .Q({Break, PCRA_Flip, Bus_Request, Addr, SPSIDI, Main}));

  // Notes on the sheet:
  //   Flags: 0: Overflow
  //   1: Sign
  //   2: Zero
  //   3: CarryA
  //   4: CarryL
  //   5: PCRA Flip
  //   6: Reset
  //   Main: 0-3: Assert A-D
  //   4-7: Load A-D
  //   SPSIDI: 0,1: Inc SPSIDI0,1
  //   Addr: 000 Memory Ack
  //   001 PCRA0
  //   010 PCRA1
  //   011 SP
  //   100 SI
  //   101 DI
  //   111 TX
  //   Bus_Request: 1: PCRA Flip
  //   2: Break
endmodule
