// Digital circuit Terminal.dig as structural Verilog
module Terminal (
  input  [7:0] D,
  input  C,
  input  Load
);

  wire not_1_out;

  not not_1 (not_1_out, C);
  Terminal terminal_1 (.D(D), .C(not_1_out), .en(Load));
endmodule
